# Fritzing sketch fan-controller-circuit (saved by Fritzing 0.9.3b)
breadboards: 1

parts:
  WeMos_D1_Mini1 = WeMos D1 Mini
  U1 = TLP621 [package=THT]
  U2 = TLP621 [package=THT]
  U3 = TLP621 [package=THT]
  U4 = TLP621 [package=THT]
  U5 = TLP621 [package=THT]
  U6 = TLP621 [package=THT]
  U7 = TLP621 [package=THT]
  U8 = TLP621 [package=THT]
  U9 = TLP621 [package=THT]
  R1 = 1k Ω Resistor [package=THT]  # not connected
  R2 = 1k Ω Resistor [package=THT]  # not connected
  R3 = 1k Ω Resistor [package=THT]  # not connected
  R4 = 1k Ω Resistor [package=THT]  # not connected
  R5 = 1k Ω Resistor [package=THT]  # not connected
  R6 = 1k Ω Resistor [package=THT]
  R7 = 1k Ω Resistor [package=THT]
  R8 = 1k Ω Resistor [package=THT]
  R9 = 1k Ω Resistor [package=THT]
  S1 = Momentary Switch [package=ksa_sealed_tac_switch]
  S2 = Momentary Switch [package=ksa_sealed_tac_switch]
  S3 = Momentary Switch [package=ksa_sealed_tac_switch]
  S4 = Momentary Switch [package=ksa_sealed_tac_switch]
  S5 = Momentary Switch [package=ksa_sealed_tac_switch]
  SW1 = DIP Switch 8 Position [package=dipswitch-08]
  J3 = Screw terminal - 2 pins [package=THT]
  J4 = Screw terminal - 2 pins [package=THT]
  JP1 = Header 4 [package=1x04-1mm-ra]
  J9 = Power Jack [package=power_jack_pth_lock]

nets:
  N1: WeMos_D1_Mini1.D5, R6.Pin_1
  N2: WeMos_D1_Mini1.D6, R7.Pin_1
  N3: WeMos_D1_Mini1.D7, R8.Pin_1
  N4: WeMos_D1_Mini1.D8, R9.Pin_1
  N5: WeMos_D1_Mini1.G, U1.Pin_2, U2.Pin_2, U3.Pin_2, U4.Pin_2, U5.Pin_2, U6.Pin_2, U7.Pin_2, U8.Pin_2, U9.Pin_2
  N6: U1.Pin_4, S1.4
  N7: U1.Pin_3, S1.2
  N8: U2.Pin_4, S2.4
  N9: U2.Pin_3, S2.2
  N10: U3.Pin_4, S3.4
  N11: U3.Pin_3, S3.2
  N12: U4.Pin_4, S4.4
  N13: U4.Pin_3, S4.2
  N14: U5.Pin_4, S5.4
  N15: U5.Pin_3, S5.2
  N16: U6.Pin_1, R6.Pin_0
  N17: U6.Pin_4, SW1.16
  N18: U6.Pin_3, SW1.1
  N19: U7.Pin_1, R7.Pin_0
  N20: U7.Pin_4, SW1.15
  N21: U7.Pin_3, SW1.2
  N22: U8.Pin_1, R8.Pin_0
  N23: U8.Pin_4, SW1.14
  N24: U8.Pin_3, SW1.3
  N25: U9.Pin_1, R9.Pin_0
  N26: U9.Pin_4, SW1.13
  N27: U9.Pin_3, SW1.4
  N28: J3.pin1, J4.pin2, JP1.3, J9.GND
  N29: J3.pin2, J4.pin1, JP1.4, J9.GNDBREAK

notes:
  Fan
  Low
  Light
  ON/OFF
  Fan
  Med.
  Fan
  High
  Fan
  Off
  Fan Selector DIP
  Battery
  Connector

custom parts:
  1k Ω Resistor: A generic resistor (0.25W)
